# Fritzing sketch skeleton_layout (saved by Fritzing 0.9.4)
breadboards: 1

parts:
  SW3 = DIP Switch 8 Position [package=dipswitch-08]
  Basic_IO_Shield1 = chipKIT Basic I/O Shield [chip_label=IC package="DIP (Dual Inline) [THT]"]
  Raspberry_Pi1 = Raspberry Pi 2  # not connected

nets:
  N1: SW3.1, SW3.2, SW3.3, SW3.4, SW3.5, SW3.6, SW3.7, SW3.8, Basic_IO_Shield1.A
  N2: SW3.9, Basic_IO_Shield1.D26
  N3: SW3.10, Basic_IO_Shield1.D27
  N4: SW3.11, Basic_IO_Shield1.D28
  N5: SW3.12, Basic_IO_Shield1.D29
  N6: SW3.13, Basic_IO_Shield1.D30
  N7: SW3.14, Basic_IO_Shield1.D31
  N8: SW3.15, Basic_IO_Shield1.D32
  N9: SW3.16, Basic_IO_Shield1.D33

custom parts:
  chipKIT Basic I/O Shield: The chipKIT Basic I/O Shield is an input/output expansion board designed for use with chipKIT microcontroller boards such as the Uno32™ and the Max32™. The Basic I/O Shield is designed to provide a range of input/output devices suitable for beginners learning about microcontrollers and various types of I/O devices, or for use by more advanced user to provide inputs or outputs for their own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
